# Fritzing sketch diagram (saved by Fritzing 0.9.5d)
breadboards: 1

parts:
  Raspberry_Pi1 = Raspberry Pi 2
  ADC1 = MCP3008 [package=dil16]
  R1 = Photocell (LDR) [package=THT]
  LCD2 = LCD screen
  LCM1602_IIC2 = LCM1602 IIC [part_number="LCM1602 IIC" chip_label="LCM1602 IIC" package="DIP (Dual Inline) [THT]"]
  R2 = Resistor [tolerance=±5% resistance=10k package="2512 [SMD]"]
  S1 = Pushbutton [package="[SMD]"]

nets:
  3V3: Raspberry_Pi1.3v3, ADC1.VREF, ADC1.VDD, R1.pin_1
  N1: Raspberry_Pi1.GPIO2, LCM1602_IIC2.SDA
  N2: Raspberry_Pi1.GPIO3, LCM1602_IIC2.SCL
  N3: Raspberry_Pi1.GPIO10, ADC1.Din
  N4: Raspberry_Pi1.GPIO9, ADC1.Dout
  N5: Raspberry_Pi1.GPIO11, ADC1.CLK
  N6: Raspberry_Pi1.GPIO8, ADC1.CS/SHDN
  N7: Raspberry_Pi1.GPIO23, S1.Pin_3, S1.Pin_4
  GND: Raspberry_Pi1.GND, ADC1.DGND, ADC1.AGND, LCM1602_IIC2.GND, R2.Pin_0, S1.Pin_1, S1.Pin_2
  5V: Raspberry_Pi1.5V, LCM1602_IIC2.VCC
  N8: ADC1.CH0, R1.pin_0, R2.Pin_1
  VSS: LCD2.VSS, LCM1602_IIC2.VSS
  VDD: LCD2.VDD, LCM1602_IIC2.VDD
  N9: LCD2.V0, LCM1602_IIC2.V0
  N10: LCD2.RS, LCM1602_IIC2.RS
  N11: LCD2.R/W, LCM1602_IIC2.RW
  N12: LCD2.E, LCM1602_IIC2.E
  N13: LCD2.DB0, LCM1602_IIC2.D0
  N14: LCD2.DB1, LCM1602_IIC2.D1
  N15: LCD2.DB2, LCM1602_IIC2.D2
  N16: LCD2.DB3, LCM1602_IIC2.D3
  N17: LCD2.DB4, LCM1602_IIC2.D4
  N18: LCD2.DB5, LCM1602_IIC2.D5
  N19: LCD2.DB6, LCM1602_IIC2.D6
  N20: LCD2.DB7, LCM1602_IIC2.D7
  N21: LCD2.LED+, LCM1602_IIC2.A
  N22: LCD2.LED-, LCM1602_IIC2.K
  N23: LCM1602_IIC2.LED_A, LCM1602_IIC2.LED_B

custom parts:
  LCM1602 IIC: I2C-Module to use a 1602 or 2004 LCD on with the wire.h libory Serial LCD Modul
